# Fritzing sketch schematic (saved by Fritzing 0.9.3b)

parts:
  Part1 = Arduino Nano (Rev3.0) (ICSP)
  Part3 = Real Time Clock Module - DS1307 RTC Breakout Board
  S1 = Pushbutton [package="[SMD]"]  # not connected
  S2 = Pushbutton [package="[SMD]"]  # not connected
  LED1 = LED - 3mm [color="Red (633nm)" package="3 mm [THT]"]  # not connected
  LED2 = LED - 3mm [color="Blue (430nm)" package="3 mm [THT]"]  # not connected
  U2 = 74HC595 [package="DIP16 [THT]"]
  R1 = Resistor [tolerance=±5% resistance=220 package="0805 [SMD]"]
  R2 = Resistor [tolerance=±5% resistance=220 package="0805 [SMD]"]
  R3 = Resistor [tolerance=±5% resistance=220 package="0805 [SMD]"]
  R4 = Resistor [tolerance=±5% resistance=220 package="0805 [SMD]"]
  U1 = 7-SEGMENT-4DIGIT-YOUNGSUN [package=7-segment-4digit-youngsun]

nets:
  GND: Part1.GND, Part3.GND, U2.GND, U2.OE, R1.Pin_1, R2.Pin_1, R3.Pin_1, R4.Pin_1
  N1: Part1.D9, U2.ST_CP
  N2: Part1.D10, U2.SH_CP
  5V: Part1.5V, Part3.5V, U2.VCC
  N3: Part1.A5, Part3.SCL
  N4: Part1.A4, Part3.SDA
  N5: U2.Q0, U1.F
  N6: R4.Pin_0, U1.COL-C
